# Fritzing sketch bluetooth.led.controller (saved by Fritzing 0.9.3b)
circuit board: 1.74119cm x 3.87735cm
breadboards: 1

parts:
  R1 = Resistor [tolerance=±5% resistance=2k package=THT]
  R2 = Resistor [tolerance=±5% resistance=1k package=THT]
  Часть1 = Arduino Uno (Rev3)
  Часть2 = Bluetooth HC-05 Macho
  R3 = Resistor [tolerance=±5% resistance=220 package=THT]
  R4 = Resistor [tolerance=±5% resistance=220 package=THT]
  R5 = Resistor [tolerance=±5% resistance=220 package=THT]
  LED1 = LED - 5mm [color="Green (555nm)" package="5 mm [THT]"]
  LED2 = LED - 5mm [color="Blue (430nm)" package="5 mm [THT]"]
  LED3 = LED - 5mm [color="Red (633nm)" package="5 mm [THT]"]

nets:
  N1: R1.Pin_0, R2.Pin_1, Часть2.RXD
  GND: R1.Pin_1, Часть1.GND, Часть2.GND, LED1.cathode, LED2.cathode, LED3.cathode
  N2: R2.Pin_0, Часть1.D11_PWM/MOSI
  N3: Часть1.D10_PWM/SS, Часть2.TXD
  N4: Часть1.D3_PWM, R3.Pin_1
  N5: Часть1.D4, R4.Pin_1
  N6: Часть1.D5_PWM, R5.Pin_1
  5V: Часть1.5V, Часть2.VCC
  N7: R3.Pin_0, LED1.anode
  N8: R4.Pin_0, LED2.anode
  N9: R5.Pin_0, LED3.anode

// code stored in the sketch: bluetooth.monitor.port.ino
#include <SoftwareSerial.h>

const byte RED_LED = 5;
const byte GREEN_LED = 4;
const byte BLUE_LED = 3;
const int VELOCITY = 200;
char state = 'f';

char incomingMessage;

SoftwareSerial HC05Module(10, 11); // TXD | RXD

void setup() {
  pinMode( RED_LED, OUTPUT );
  pinMode( GREEN_LED, OUTPUT );
  pinMode( BLUE_LED, OUTPUT );

  Serial.begin(9600);
  HC05Module.begin(9600);  //Default Baud for comm, it may be different for your Module.
  Serial.println("The bluetooth gates are open.");
}

void loop() {
  // Feed any data from bluetooth to Terminal.
  if (HC05Module.available()) {
    incomingMessage = HC05Module.read();
    Serial.println(incomingMessage);

    switch (incomingMessage) {
      case 'r':
        Serial.println("RED");
        state = 'r';
        ledSwitch(RED_LED);
        HC05Module.println("RED");
        break;
      case 'g':
        Serial.println("GREEN");
        state = 'g';
        ledSwitch(GREEN_LED);
        HC05Module.println("GREEN");
        break;
      case 'b':
        Serial.println("BLUE");
        state = 'b';
        ledSwitch(BLUE_LED);
        HC05Module.println("BLUE");
        break;
      case 'f':
        Serial.println("OFF");
        state = 'f';
        ledsOff();
        HC05Module.println("OFF");
        break;
      case 'w':
        Serial.println("RAINBOW");
        ledsOff();
        if (state == 'w') state = 'f';
        else state = 'w';
        HC05Module.println("RAINBOW");
        break;
    }
  }
  if (Serial.available())    HC05Module.write(Serial.read());
  if (state == 'w') rainbow();
}

void ledSwitch(byte led) {
  if (!digitalRead(led))digitalWrite( led, HIGH );
  else digitalWrite( led, LOW );
}

void ledsOff() {
  digitalWrite( RED_LED, LOW );
  digitalWrite( GREEN_LED, LOW );
  digitalWrite( BLUE_LED, LOW );
}

void rainbow() {
  digitalWrite( RED_LED, HIGH );
  delay(VELOCITY);
  digitalWrite( RED_LED, LOW );
  digitalWrite( GREEN_LED, HIGH );
  delay(VELOCITY);
  digitalWrite( GREEN_LED, LOW );
  digitalWrite( BLUE_LED, HIGH );
  delay(VELOCITY);
  digitalWrite( BLUE_LED, LOW );
  delay(VELOCITY);
  digitalWrite( RED_LED, HIGH );
  digitalWrite( GREEN_LED, HIGH );
  digitalWrite( BLUE_LED, LOW );
  delay(VELOCITY);
  digitalWrite( RED_LED, LOW );
  digitalWrite( GREEN_LED, HIGH );
  digitalWrite( BLUE_LED, HIGH );
  delay(VELOCITY);
  digitalWrite( RED_LED, HIGH );
  digitalWrite( GREEN_LED, LOW );
  digitalWrite( BLUE_LED, HIGH );
  delay(VELOCITY);
  digitalWrite( RED_LED, HIGH );
  digitalWrite( GREEN_LED, HIGH );
  digitalWrite( BLUE_LED, LOW );
  delay(VELOCITY);
  digitalWrite( RED_LED, LOW );
  digitalWrite( GREEN_LED, LOW );
  digitalWrite( BLUE_LED, LOW );
}
