# Fritzing sketch bluetooth.monitor.port (saved by Fritzing 0.9.3b)
circuit board: 1.74119cm x 3.87735cm
breadboards: 1

parts:
  R1 = Resistor [tolerance=±5% resistance=2k package=THT]
  R2 = Resistor [tolerance=±5% resistance=1k package=THT]
  Часть1 = Arduino Uno (Rev3)
  Часть2 = Bluetooth HC-05 Macho

nets:
  N1: R1.Pin_0, R2.Pin_1, Часть2.RXD
  GND: R1.Pin_1, Часть1.GND, Часть2.GND
  N2: R2.Pin_0, Часть1.D11_PWM/MOSI
  N3: Часть1.D10_PWM/SS, Часть2.TXD
  5V: Часть1.5V, Часть2.VCC

// code stored in the sketch: bluetooth.monitor.port.ino
#include <SoftwareSerial.h>

SoftwareSerial HC05Module(10, 11); // TXD | RXD

void setup() {
  Serial.begin(9600);
  HC05Module.begin(9600);  //Default Baud for comm, it may be different for your Module.
  Serial.println("The bluetooth gates are open.");

}

void loop() {
  // Feed any data from bluetooth to Terminal.
  if (HC05Module.available())
    Serial.write(HC05Module.read());

  // Feed all data from termial to bluetooth
  if (Serial.available())
    HC05Module.write(Serial.read());

}
