# Fritzing sketch led.strip.rainbow (saved by Fritzing 0.9.3b)
breadboards: 1

parts:
  Part1 = Arduino Uno (Rev3)
  U1 = WS2812 RGB LED strip
  C1 = Electrolytic Capacitor [capacitance=1mF package="100 mil [THT, electrolytic]"]
  R1 = Resistor [tolerance=±5% resistance=200k package=THT]
  VCC1 = Battery

nets:
  N1: Part1.D13/SCK, U1.DOUT, R1.Pin_0, R1.Pin_1
  GND: Part1.GND, U1.GND, C1.+, VCC1.-
  N2: U1.VCC, C1.-, VCC1.+

notes:
  200 - 500 kOm

custom parts:
  WS2812 RGB LED strip: WS2812 strip

// code stored in the sketch: led.strip.rainbow.ino
#define NUM_LEDS 12
#include "FastLED.h"
#define PIN 13
CRGB leds[NUM_LEDS];
byte counter;
void setup() {
  FastLED.addLeds<WS2811, PIN, GRB>(leds, NUM_LEDS).setCorrection( TypicalLEDStrip );
  FastLED.setBrightness(50);
  pinMode(13, OUTPUT);
}
void loop() {
  for (int i = 0; i < NUM_LEDS; i++ ) {
    leds[i] = CHSV(counter + i * 2, 255, 255);
  }
  counter++;
  FastLED.show();
  delay(5);
}
