# Fritzing sketch dc.motor.l293d (saved by Fritzing 0.9.3b)
breadboards: 1

parts:
  Part1 = Arduino Uno (Rev3)
  IC1 = L293D [package=THT]
  M1 = DC Motor
  VCC1 = Battery block 9V

nets:
  N1: Part1.D2, IC1.In_4
  N2: Part1.D3_PWM, IC1.In_3
  N3: Part1.D5_PWM, IC1.Enable_2
  N4: Part1.5V, VCC1.-
  N5: Part1.GND, IC1.0V, IC1.+Vmotor
  N6: IC1.Out_3_(_Controlled_by_Enable_2_), M1.pin_2
  N7: IC1.Out_4_(_Controlled_by_Enable_2_), M1.pin_1
  N8: IC1.+V, VCC1.+

// code stored in the sketch: dc.motor.l293d.ino
const int in3 = 2;
const int in4 = 3;
const int en2 = 5;

const int FORWARD = 23240;
const int BACKWARD = 30410;
const int STOP = 7140;

void setup() {
  pinMode(in3, OUTPUT);
  pinMode(in4, OUTPUT);
  pinMode(en2, OUTPUT);

  analogWrite(en2, 255);

  Serial.begin(9600);
}

void loop() {
  if (Serial.available() > 0) {
    switch (getStringInt() ) {
      case FORWARD:
        drive(HIGH, LOW);
        break;
      case BACKWARD:
        drive(LOW, HIGH);
        break;
      case STOP:
        drive(LOW, LOW);
        break;
    }
  }

}

void drive(boolean forward, boolean backward) {
  digitalWrite(in3, forward);
  digitalWrite(in4, backward);
  
}

int getStringInt() {
  String incomingString = Serial.readString();
  int stringInt = 0;

  for (int i = 0; incomingString[i] != 0; i++) {
    stringInt += int(incomingString[i]) * i * 10;
  };

  return stringInt;
}
